// Logisim project SAP1_DDanielTerra.circ as structural Verilog: 11 circuits, main circuit main
module main (
  input  Reset,
  input  mem,
  output [3:0] Dados,
  output [3:0] \Dados___Endereços ,
  output out_5,
  output out_6,
  output out_7,
  output out_8,
  output out_9,
  output out_10,
  output out_11,
  output out_12
);

  wire Ar, CLK, Clock_out, controlador_sequencializador_rom_1_hlt, Cp, Dec, Ea, Ep, Eu, Inc, Lp, Mul, nCE,
       nEi, nLa, nLb, nLi, nLm, nLo, not_1_out, not_2_out, not_3_out, not_4_out,
       \registrador_instruções_1_i4 , \registrador_instruções_1_i5 , \registrador_instruções_1_i6 ,
       \registrador_instruções_1_i7 , Su;
  wire [3:0] rem_1_remout;
  wire [7:0] acumulador_1_a_out_ula, counter_1_q, registrador_b_1_b_dataout, Sv;

  Clock Clock (.out(Clock_out));
  not not_1 (not_1_out, CLK);
  not not_2 (not_2_out, Reset);
  not not_3 (not_3_out, nCE);
  assign CLK = not_4_out ? Clock_out : 1'bz;  // Controlled_Buffer controlled_buffer_1
  not not_4 (not_4_out, controlador_sequencializador_rom_1_hlt);
  REM rem_1 (.in_1(\Dados___Endereços ), .nLm(nLm), .CLK(CLK), .REMOut(rem_1_remout));
  Contador_Programa contador_programa_1 (
    .Cp(Cp), .nCLK(not_1_out), .nCLR(not_2_out), .Ep(Ep), .Cp_Out(\Dados___Endereços ), .Ar(Ar),
    .Cp_In(\Dados___Endereços ));
  \Memória_RAM  \memória_ram_1  (
    .in_1(rem_1_remout), .nCE(not_3_out), .CLK(CLK), .out_6({Dados, \Dados___Endereços }), .in_2(Sv));  // open: Sv
  \Registrador_Instruções  \registrador_instruções_1  (
    .in_1({Dados, \Dados___Endereços }), .nLi(nLi), .CLK(CLK), .CLR(Reset), .nEi(nEi),
    .out_6(\Dados___Endereços ), .I4(\registrador_instruções_1_i4 ), .I5(\registrador_instruções_1_i5 ),
    .I6(\registrador_instruções_1_i6 ), .I7(\registrador_instruções_1_i7 ));
  Controlador_Sequencializador_ROM controlador_sequencializador_rom_1 (
    .CLK(CLK), .CLR(Reset), .HLT(controlador_sequencializador_rom_1_hlt), .Cp(Cp), .Ep(Ep), .nLm(nLm),
    .nCE(nCE), .nLl(nLi), .nEl(nEi), .nLa(nLa), .Ea(Ea), .Su(Su), .Eu(Eu), .nLb(nLb), .nLo(nLo),
    .I7(\registrador_instruções_1_i7 ), .I6(\registrador_instruções_1_i6 ),
    .I4(\registrador_instruções_1_i4 ), .Inc(Inc), .Dec(Dec), .Mul(Mul), .Lp(Lp),
    .I5(\registrador_instruções_1_i5 ));
  Acumulador acumulador_1 (
    .A_In({Dados, \Dados___Endereços }), .nLa(nLa), .CLK(CLK), .Ea(Ea), .A_Out_ULA(acumulador_1_a_out_ula),
    .A_Out({Dados, \Dados___Endereços }));
  Somador_Subtrator somador_subtrator_1 (
    .Su(Su), .B_data(registrador_b_1_b_dataout), .A_dataOut2({Dados, \Dados___Endereços }),
    .A_data(acumulador_1_a_out_ula), .Eu(Eu), .inc(Inc), .dec(Dec), .mul(Mul));
  Registrador_B registrador_b_1 (
    .B_dataIn({Dados, \Dados___Endereços }), .B_dataOut(registrador_b_1_b_dataout), .nLb(nLb), .CLK(CLK));
  Hex_Digit_Display hex_digit_display_1 (.value({out_5, out_6, out_7, out_8}));  // open: dp
  \Indicação_Visual  \indicação_visual_1  (
    .Input({Dados, \Dados___Endereços }),
    .Output({out_5, out_6, out_7, out_8, out_9, out_10, out_11, out_12}), .nLo(nLo), .CLK(CLK), .CLR(Reset),
    .mem(mem));  // open: mem_2
  Hex_Digit_Display hex_digit_display_2 (.value({out_9, out_10, out_11, out_12}));  // open: dp
  DotMatrix #(.matrixcols(8), .matrixrows(1), .dotshape("circle")) dotmatrix_1 (
    .col0(out_5), .col1(out_6), .col2(out_7), .col3(out_8), .col4(out_9), .col5(out_10), .col6(out_11),
    .col7(out_12));
  Counter counter_1 (.Q(counter_1_q), .clk(CLK), .clr(Reset));  // open: load, D, count, carry
  Hex_Digit_Display hex_digit_display_3 (.value(counter_1_q[7:4]));  // open: dp
  Hex_Digit_Display hex_digit_display_4 (.value(counter_1_q[3:0]));  // open: dp

  // Other names for the same wires on the sheet: CLR = Reset

  // Notes on the sheet:
  //   SAP-1 EM LOGISIM Modificado
  //   Arquitetura de Computadores I
  //   Daniel Meireles Terra
  //   CC - Ciencias da computação
  //   Orientador: Prof. Dr. Cláudio Dias Campos. 
  //   Grupo:
  //   Instruções:
  //   LDA 0000: A<-*(MEM)
  //   ADD 0001: A<-A+B
  //   SUB 0010: A<-A-B
  //   INC 0011: A<=A+1
  //   DEC 0100: A<=A-1
  //   MUL 0101: A<-AxB
  //   JMP 0110: CP<-endereço de salto
  //   OUT 1110: exibir o valor
  //   HLT 1111: interromper o circuito
  //   Como usar:
  //   Adicione as operações no bloco de memória RAM,
  //   execute um RESET e envie pulsos de clock.
  //   Esse trabalho foi uma modificação do trabalho feito por:
  //   - André Luís Silva de Paula
  //   - André Santos Alves
  //   - Nathan de Araújo Cunha Lisboa
  //   - Pedro Malta Boscatti
  //   - Sophia Damasceno Satuf
  //   As modificações foram feitas no controlador sequencializador.
  //   Com as alterações agora o controlador é implementado usando
  //   ROMs e possui ciclo variavél de máquina.
endmodule

module Contador_Programa (
  input  Ar,
  input  [3:0] Cp_In,
  input  Cp,
  input  nCLK,
  input  nCLR,
  input  Ep,
  output [3:0] Cp_Out
);

  wire not_1_out;
  wire [3:0] counter_1_q;

  not not_1 (not_1_out, nCLR);
  Counter #(.width(4), .max('hf), .trigger("falling")) counter_1 (
    .load(Ar), .D(Cp_In), .count(Cp), .Q(counter_1_q), .clk(nCLK), .clr(not_1_out));  // open: carry
  assign Cp_Out = Ep ? counter_1_q : 4'bz;  // Controlled_Buffer controlled_buffer_1
endmodule

module REM (
  input  [3:0] in_1,
  input  nLm,
  input  CLK,
  output [3:0] REMOut
);

  wire not_1_out;

  not not_1 (not_1_out, nLm);
  Register #(.width(4)) register_1 (.D(in_1), .en(not_1_out), .Q(REMOut), .clk(CLK));  // open: clr
endmodule

module \Memória_RAM  (
  input  [3:0] in_1,
  input  [7:0] in_2,
  input  nCE,
  input  CLK,
  input  Sv,
  output [7:0] out_6
);

  wire and_1_out, not_1_out, or_1_out;
  wire [7:0] ram_1_data;

  D_Flip_Flop d_ff_1 ();  // open: clk, D, Q, Qn, preset, en, reset
  or or_1 (or_1_out, Sv, nCE);
  RAM #(.addrWidth(4)) ram_1 (.addr(in_1), .data(ram_1_data), .sel(or_1_out), .clk(CLK), .ld(and_1_out));  // open: clr
  and and_1 (and_1_out, nCE, not_1_out);
  not not_1 (not_1_out, Sv);
  assign out_6 = nCE ? ram_1_data : 8'bz;  // Controlled_Buffer controlled_buffer_1
  assign ram_1_data = Sv ? in_2 : 8'bz;  // Controlled_Buffer controlled_buffer_2
endmodule

module \Registrador_Instruções  (
  input  [7:0] in_1,
  input  nLi,
  input  CLK,
  input  CLR,
  input  nEi,
  output [3:0] out_6,
  output I4,
  output I5,
  output I6,
  output I7
);

  wire not_1_out, not_2_out;
  wire [3:0] register_1_q;

  not not_1 (not_1_out, nLi);
  not not_2 (not_2_out, nEi);
  Register register_1 (.D(in_1), .en(not_1_out), .Q({I7, I6, I5, I4, register_1_q}), .clk(CLK), .clr(CLR));
  assign out_6 = not_2_out ? register_1_q : 4'bz;  // Controlled_Buffer controlled_buffer_1
endmodule

module Acumulador (
  input  [7:0] A_In,
  input  nLa,
  input  CLK,
  input  Ea,
  output [7:0] A_Out_ULA,
  output [7:0] A_Out
);

  wire not_1_out;

  not not_1 (not_1_out, nLa);
  Register register_1 (.D(A_In), .en(not_1_out), .Q(A_Out_ULA), .clk(CLK));  // open: clr
  assign A_Out = Ea ? A_Out_ULA : 8'bz;  // Controlled_Buffer controlled_buffer_1
endmodule

module Somador_Subtrator (
  input  Su,
  input  inc,
  input  dec,
  input  [7:0] B_data,
  input  [7:0] A_data,
  input  Eu,
  input  mul,
  output [7:0] A_dataOut2
);

  wire not_1_out, or_1_out;
  wire [7:0] adder_1_out, controlled_buffer_1_out, multiplier_1_out, xor_1_out;

  or or_1 (or_1_out, inc, dec);
  not not_1 (not_1_out, or_1_out);
  assign controlled_buffer_1_out = or_1_out ? 8'h1 : 8'bz;  // Controlled_Buffer controlled_buffer_1
  assign controlled_buffer_1_out = not_1_out ? B_data : 8'bz;  // Controlled_Buffer controlled_buffer_2
  assign xor_1_out = {8{Su}} ^ controlled_buffer_1_out;  // XOR_Gate xor_1, 8 bits wide
  Adder adder_1 (.a(xor_1_out), .b(A_data), .out(adder_1_out), .cin(Su));  // open: cout
  Multiplier multiplier_1 (.a(B_data), .b(A_data), .out(multiplier_1_out));  // open: cin, cout
  assign A_dataOut2 = Eu ? adder_1_out : 8'bz;  // Controlled_Buffer controlled_buffer_3
  assign A_dataOut2 = mul ? multiplier_1_out : 8'bz;  // Controlled_Buffer controlled_buffer_4
endmodule

module Registrador_B (
  input  [7:0] B_dataIn,
  input  nLb,
  input  CLK,
  output [7:0] B_dataOut
);

  wire not_1_out;

  Register register_1 (.D(B_dataIn), .en(not_1_out), .Q(B_dataOut), .clk(CLK));  // open: clr
  not not_1 (not_1_out, nLb);
endmodule

module Decodificador (
  input  l7,
  input  l6,
  input  l5,
  input  l4,
  output LDA,
  output ADD,
  output SUB,
  output OUT,
  output HLT
);

  wire and_1_out, and_2_out, and_3_out, and_4_out, and_5_out, not_1_out, not_2_out, not_3_out, not_4_out;

  not not_1 (not_1_out, l7);
  not not_2 (not_2_out, l6);
  not not_3 (not_3_out, l5);
  not not_4 (not_4_out, l4);
  buf buffer_1 (LDA, and_1_out);
  and and_1 (and_1_out, not_1_out, not_2_out, not_3_out, not_4_out);
  buf buffer_2 (ADD, and_2_out);
  and and_2 (and_2_out, not_1_out, not_2_out, not_3_out, l4);
  and and_3 (and_3_out, not_1_out, not_2_out, l5, not_4_out);
  buf buffer_3 (SUB, and_3_out);
  buf buffer_4 (OUT, and_4_out);
  and and_4 (and_4_out, l7, l6, l5, not_4_out);
  buf buffer_5 (HLT, and_5_out);
  and and_5 (and_5_out, l7, l6, l5, l4);
endmodule

module \Indicação_Visual  (
  input  mem,
  input  [7:0] Input,
  input  nLo,
  input  CLK,
  input  CLR,
  input  mem_2,
  output [7:0] Output
);

  wire controlled_buffer_1_out, not_1_out, not_2_out, not_3_out, not_4_out, or_1_out;
  wire [7:0] d_ff_1_q, register_1_q;

  assign controlled_buffer_1_out = not_1_out ? mem : 1'bz;  // Controlled_Buffer controlled_buffer_1
  not not_1 (not_1_out, or_1_out);
  not not_2 (not_2_out, controlled_buffer_1_out);
  assign controlled_buffer_1_out = not_2_out ? or_1_out : 1'bz;  // Controlled_Buffer controlled_buffer_2
  or or_1 (or_1_out, Input[0], Input[1], Input[2], Input[3], Input[4], Input[5], Input[6], Input[7]);
  D_Flip_Flop d_ff_1 (.clk(mem_2), .D(Input[0]), .Q(d_ff_1_q[0]));  // open: Qn, preset, en, reset
  D_Flip_Flop d_ff_2 (.clk(mem_2), .D(Input[1]), .Q(d_ff_1_q[1]));  // open: Qn, preset, en, reset
  D_Flip_Flop d_ff_3 (.clk(mem_2), .D(Input[2]), .Q(d_ff_1_q[2]));  // open: Qn, preset, en, reset
  D_Flip_Flop d_ff_4 (.clk(mem_2), .D(Input[3]), .Q(d_ff_1_q[3]));  // open: Qn, preset, en, reset
  D_Flip_Flop d_ff_5 (.clk(mem_2), .D(Input[4]), .Q(d_ff_1_q[4]));  // open: Qn, preset, en, reset
  D_Flip_Flop d_ff_6 (.clk(mem_2), .D(Input[5]), .Q(d_ff_1_q[5]));  // open: Qn, preset, en, reset
  D_Flip_Flop d_ff_7 (.clk(mem_2), .D(Input[6]), .Q(d_ff_1_q[6]));  // open: Qn, preset, en, reset
  D_Flip_Flop d_ff_8 (.clk(mem_2), .D(Input[7]), .Q(d_ff_1_q[7]));  // open: Qn, preset, en, reset
  Register register_1 (.D(Input), .en(not_3_out), .Q(register_1_q), .clk(CLK), .clr(CLR));
  not not_3 (not_3_out, nLo);
  assign Output = not_4_out ? register_1_q : 8'bz;  // Controlled_Buffer controlled_buffer_3
  not not_4 (not_4_out, mem);
  assign Output = mem ? d_ff_1_q : 8'bz;  // Controlled_Buffer controlled_buffer_4

  // Notes on the sheet:
  //   Ouve um erro. não identificado
endmodule

module Controlador_Sequencializador_ROM (
  input  I7,
  input  I6,
  input  I5,
  input  I4,
  input  CLK,
  input  CLR,
  output Cp,
  output Ep,
  output nLm,
  output nCE,
  output nLl,
  output nEl,
  output nLa,
  output Ea,
  output Su,
  output Eu,
  output nLb,
  output nLo,
  output Inc,
  output Dec,
  output Mul,
  output Lp,
  output HLT
);

  wire and_2_out, and_3_out, and_5_out, and_6_out, clr_t, load, nop, nor_1_out, not_1_out, not_2_out,
       or_1_out, shift_register_1_q0, shift_register_1_q1, shift_register_1_q3, shift_register_1_q4;
  wire [4:0] counter_1_q, rom_1_data;

  and and_1 (HLT, I7, I6, I5, I4);
  ROM #(.addrWidth(4), .dataWidth(5)) rom_1 (.addr({I7, I6, I5, I4}), .data(rom_1_data));  // open: sel
  or or_1 (or_1_out, CLR, nop);
  or or_2 (clr_t, or_1_out, nor_1_out);
  not not_1 (not_1_out, load);
  not not_2 (not_2_out, CLK);
  Shift_Register #(.length(6)) shift_register_1 (
    .in(nor_1_out), .clk(CLK), .clr(or_1_out), .q0(shift_register_1_q0), .q1(shift_register_1_q1), .q2(load),
    .q3(shift_register_1_q3), .q4(shift_register_1_q4));  // open: shift, out, load, d0, d1, d2, d3, d4, d5, q5
  Counter #(.width(5), .max('h1f), .ongoal("continue")) counter_1 (
    .load(load), .D(rom_1_data), .count(not_1_out), .Q(counter_1_q), .clk(not_2_out), .clr(clr_t));  // open: carry
  nor nor_1 (nor_1_out, shift_register_1_q0, shift_register_1_q1, load, shift_register_1_q3, shift_register_1_q4);
  ROM #(.addrWidth(5), .dataWidth(16)) rom_2 (
    .addr(counter_1_q), .data({Cp, Ep, nLm, nCE, nLl, nEl, nLa, Ea, Su, Eu, nLb, nLo, Inc, Dec, Mul, Lp}));  // open: sel
  and and_2 (and_2_out, ~Cp, ~Ep, nLm, nCE);  // AND_Gate
  and and_3 (and_3_out, nLl, nEl, nLa, ~Ea);  // AND_Gate
  and and_4 (nop, and_2_out, and_3_out, and_5_out, and_6_out);
  and and_5 (and_5_out, ~Su, ~Eu, nLb, nLo);  // AND_Gate
  and and_6 (and_6_out, ~Inc, ~Dec, ~Mul, ~Lp);  // AND_Gate

  // Notes on the sheet:
  //   contents of rom_1 (hex, n*v repeats v):
  //   3 6 9 10 13 16 19 7*0 c
  //   contents of rom_2 (hex, n*v repeats v):
  //   5e30 be30 2630 1a30 2c30 3e30 1a30 2e10 3c70 1a30 2e10 3cf0 3f20 3e30 3e30 0 3c78 3e30 3e30 3cf4
  //   3e30 3e30 1a30 2e10 3c32 3a31 3e30 3e30
endmodule
